# Fritzing sketch platine (saved by Fritzing 0.9.3b)
stripboards: 1

parts:
  J4 = male pin header, 2 pins [form="♂ (male)"]
  U1 = NodeMCU V1.0
  J7 = male pin header, 8 pins [form="♂ (male)"]
  DFPlayer_Mini1 = DFPlayer MINI [package="DIP (Dual Inline) [THT]"]
  J3 = screw terminal, 2 pins
  J8 = male pin header, 2 pins [form="♂ (male)"]
  R1 = Resistor [tolerance=±5% resistance=50 package=THT]

nets:
  N1: J4.pin1, U1.D3, U1.SD3, J7.pin1
  N2: J4.pin2, U1.SD2
  N3: U1.D1, DFPlayer_Mini1.TX
  N4: U1.D2, U1.RSV#40, DFPlayer_Mini1.RX
  N5: U1.D4, J7.pin2
  N6: U1.3V3, J7.pin3
  N7: U1.GND, J7.pin4, DFPlayer_Mini1.GND#9, J8.pin1
  N8: U1.D5, J7.pin5
  N9: U1.D6, J7.pin6
  N10: U1.D7, J7.pin7
  N11: U1.D8, J7.pin8
  VIN: U1.Vin, DFPlayer_Mini1.VCC, J8.pin2
  N12: DFPlayer_Mini1.SPK1, J3.pin1, R1.Pin_1
  N13: J3.pin2, R1.Pin_0

custom parts:
  NodeMCU V1.0: ESP8266 based NodeMCU
  DFPlayer MINI: MP3 module by DFRobot.com for playing Music from an SD-Card. Supports WAV and MP3 files.
